// Logisim project Guia_0501.circ as structural Verilog: 1 circuit, main circuit main
module main (
  output out_1
);

  wire nor_1_out, nor_2_out, switch_1_p1, undriven;

  // Switch switch_1: pin names not known; wires that end beside it: switch_1_p1
  nor nor_1 (nor_1_out, undriven, undriven);
  // Switch b: pin names not known
  nor nor_2 (nor_2_out, nor_1_out, switch_1_p1);
  nor nor_3 (out_1, nor_2_out, nor_2_out);
endmodule
