// Logisim project Guia_0502.circ as structural Verilog: 1 circuit, main circuit main
module main (
  output s
);

  wire a_p1, b_p1, nand_1_out, nand_2_out;

  // Switch b: pin names not known; wires that end beside it: b_p1
  nand nand_1 (nand_1_out, b_p1, b_p1);
  // Switch a: pin names not known; wires that end beside it: a_p1
  nand nand_2 (nand_2_out, a_p1, nand_1_out);
  nand nand_3 (s, nand_2_out, nand_2_out);
endmodule
