// Logisim project Guia_0505.circ as structural Verilog: 1 circuit, main circuit main
module main (
  input  a,
  input  b
);

  wire nor_1_out, nor_2_out, nor_3_out, nor_4_out, nor_5_out;

  nor nor_1 (nor_1_out, a, nor_4_out);
  nor nor_2 (nor_2_out, a, a);
  nor nor_3 (nor_3_out, nor_2_out, b);
  nor nor_4 (nor_4_out, b, b);
  nor nor_5 (nor_5_out, nor_1_out, nor_3_out);
  // NOR_Gate nor_6 has open pins: in0=nor_5_out, in1=nor_5_out, out=open
endmodule
