// Logisim project Guia_0507.circ as structural Verilog: 1 circuit, main circuit main
module main (
  input  a,
  input  b,
  output s
);

  wire nor_1_out, nor_3_out, nor_4_out, nor_5_out;

  nor nor_1 (nor_1_out, b, b);
  nor nor_2 (b, a, a);
  nor nor_3 (nor_3_out, nor_4_out, a);
  nor nor_4 (nor_4_out, b, b);
  nor nor_5 (nor_5_out, nor_1_out, nor_3_out);
  nor nor_6 (s, nor_5_out, nor_5_out);
endmodule
