// Logisim project Guia_0508.circ as structural Verilog: 1 circuit, main circuit main
module main (
  input  a,
  input  in_2,
  output out_3
);

  wire nand_1_out;

  nand nand_1 (nand_1_out, in_2, a);
  nand nand_2 (out_3, nand_1_out, nand_1_out);
endmodule
