// Logisim project Guia_0801.circ as structural Verilog: 1 circuit, main circuit main
module main (
  input  b4,
  input  a4,
  input  b3,
  input  a3,
  input  b2,
  input  a2,
  input  b1,
  input  a1,
  input  b0,
  input  a0,
  output s05,
  output s04,
  output s03,
  output s02,
  output s01,
  output s00
);

  wire fa_1_p4, fa_2_p4, fa_3_p4, fa_4_p4;

  // FA fa_1: pin names not known; wires that end beside it: b4, a4, s05, fa_1_p4, s04
  // FA fa_2: pin names not known; wires that end beside it: b3, a3, fa_1_p4, fa_2_p4, s03
  // FA fa_3: pin names not known; wires that end beside it: b2, a2, fa_2_p4, fa_3_p4, s02
  // FA fa_4: pin names not known; wires that end beside it: b1, a1, fa_3_p4, fa_4_p4, s01
  // FA fa_5: pin names not known; wires that end beside it: b0, a0, fa_4_p4, 1'b0, s00

  // Notes on the sheet:
  //   Vinicius Miranda de Araujo - 812839$Guia_0801$Somador Completo de 5 bits
  //   "vai-um" = 0
endmodule
