// Logisim project Guia_0802.circ as structural Verilog: 1 circuit, main circuit main
module main (
  input  b5,
  input  a5,
  input  b4,
  input  a4,
  input  b3,
  input  a3,
  input  b2,
  input  a2,
  input  b1,
  input  a1,
  input  b0,
  input  a0,
  output s06,
  output s05,
  output s04,
  output s03,
  output s02,
  output s01,
  output s00
);

  wire fd_1_p4, fd_2_p4, fd_3_p4, fd_4_p4, fd_5_p4;

  // FD fd_1: pin names not known; wires that end beside it: b5, a5, s06, fd_1_p4, s05
  // FD fd_2: pin names not known; wires that end beside it: b4, a4, fd_1_p4, fd_2_p4, s04
  // FD fd_3: pin names not known; wires that end beside it: b3, a3, fd_2_p4, fd_3_p4, s03
  // FD fd_4: pin names not known; wires that end beside it: b2, a2, fd_3_p4, fd_4_p4, s02
  // FD fd_5: pin names not known; wires that end beside it: b1, a1, fd_4_p4, fd_5_p4, s01
  // FD fd_6: pin names not known; wires that end beside it: b0, a0, fd_5_p4, 1'b0, s00

  // Notes on the sheet:
  //   Vinicius Miranda de Araujo - 812839$Guia_0802$Subtrator Completo de 6 bits
  //   "vem-um" = 0
endmodule
