// Logisim project Guia_0804.circ as structural Verilog: 1 circuit, main circuit main
module main (
  input  b5,
  input  a5,
  input  b4,
  input  a4,
  input  b3,
  input  a3,
  input  b2,
  input  a2,
  input  b1,
  input  a1,
  input  b0,
  input  a0,
  output s05,
  output s04,
  output s03,
  output s02,
  output s01,
  output s00
);

  // IC ic_1: pin names not known; wires that end beside it: b5, a5, s05
  // IC ic_2: pin names not known; wires that end beside it: b4, a4, s04
  // IC ic_3: pin names not known; wires that end beside it: b3, a3, s03
  // IC ic_4: pin names not known; wires that end beside it: b2, a2, s02
  // IC ic_5: pin names not known; wires that end beside it: b1, a1, s01
  // IC ic_6: pin names not known; wires that end beside it: b0, a0, s00

  // Notes on the sheet:
  //   Vinicius Miranda de Araujo - 812839$Guia_0804$Comparador de Desigualdade de 6 bits
endmodule
